// Digital circuit pong.dig as structural Verilog
module pong (
  input  Master_VGA_Clock,
  input  Paddle,
  input  in_3,
  input  in_4,
  input  Ball_CLK
);

  wire _7408_1_pin3, _7408_1_pin6, _7408_1_pin8, _7408_1_pin11, _7408_2_pin3, _7408_2_pin4, _7408_2_pin6,
       _7408_2_pin8, _7408_2_pin9, _7408_2_pin10, _7408_2_pin12, _7408_3_pin3, _7408_3_pin6, _7408_3_pin8,
       _7408_3_pin9, _7408_3_pin11, _7408_3_pin12, _7408_4_pin3, _7408_4_pin4, _7408_4_pin6, _7408_4_pin8,
       _7408_4_pin9, _7408_4_pin10, _7408_4_pin12, _7408_5_pin2, _7408_5_pin3, _7408_5_pin6, _7408_5_pin9,
       _7408_6_pin3, _7408_6_pin8, _7430_1_pin6, _7430_1_pin8, _7430_1_pin11, _7430_1_pin12, _7430_2_pin1,
       _7430_2_pin2, _7430_2_pin3, _7430_2_pin4, _7430_2_pin6, _7430_2_pin8, _7430_2_pin12, _7430_3_pin1,
       _7430_3_pin2, _7430_3_pin3, _7430_3_pin4, _7430_3_pin8, _7430_4_pin1, _7430_4_pin2, _7430_4_pin5,
       _7430_4_pin6, _7430_4_pin8, _7430_4_pin11, _7430_4_pin12, _7430_5_pin8, _7430_6_pin8, _7430_7_pin8,
       _7430_7_pin12, _7430_8_pin8, _7430_9_pin8, _7430_10_pin1, _7430_10_pin2, _7430_10_pin3, _7430_10_pin4,
       _7430_10_pin5, _7430_10_pin6, _7430_10_pin8, _7430_10_pin11, _7430_11_pin1, _7430_11_pin2,
       _7430_11_pin3, _7430_11_pin4, _7430_11_pin5, _7474_2_pin10, _7474_2_pin13, _7474_3_pin10,
       _7474_3_pin13, _74163_1_pin15, _74163_2_pin15, _74163_4_pin15, _74163_5_pin15, _74163_7_pin1,
       _74163_7_pin15, _74163_8_pin12, _74163_9_pin15, _74163_10_pin12, _74193_1_pin11, _74193_1_pin12,
       _74193_1_pin13, _74193_2_pin12, _74193_2_pin13, _74193_4_pin11, _74193_4_pin12, _74193_4_pin13,
       _74193_5_pin12, _74193_5_pin13, _747266_1_pin3, _747266_1_pin4, _747266_1_pin10, _747266_1_pin11,
       _747266_2_pin3, _747266_2_pin4, _747266_2_pin10, _747266_2_pin11, _747266_3_pin3, _747266_3_pin4,
       _747266_3_pin10, _747266_3_pin11, A_out, add_1_c_o, add_2_c_o, and_1_out, and_2_out, and_3_out,
       and_4_out, B, ballR, bR, H0, H1, H2, H3, H4, H5, H6, H7, H8, H9, H10, H11, HCLR, HSYNC, LDOW, LUP, MO,
       nand_1_out, nand_2_out, not_1_out, not_2_out, not_3_out, not_4_out, not_16_out, not_17_out,
       not_22_out, not_24_out, not_38_out, not_39_out, not_40_out, not_41_out, not_42_out, not_43_out,
       not_44_out, not_53_out, not_54_out, not_55_out, not_56_out, not_57_out, not_58_out, not_60_out, p1R,
       p1rx, p1ry, p2R, p2rx, p2ry, RDOW, RENDER, RESET, rs_ff_as_1_q, rs_ff_as_2_q, RUP, START, V0, V1, V2,
       V3, V4, V5, V6, V7, V8, V9, V10, V11, VCLR, VSYNC, XDir_q, xnor_1_out, xnor_2_out, xnor_3_out,
       xnor_4_out, xnor_5_out, xnor_6_out, xnor_7_out, xnor_8_out, xnor_9_out, xnor_10_out, xnor_11_out,
       xnor_12_out, xnor_13_out, xnor_14_out, xnor_15_out, xnor_16_out, xnor_17_out, xnor_18_out,
       xnor_19_out, Y1D, Y1U, Y2D, Y2U, Y10, Y11, Y12, Y13, Y14, Y15, Y16, Y17, Y18, Y19, Y20, Y21, Y22, Y23,
       Y24, Y25, Y26, Y27, Y28, Y29, YDir_q, YS0, YS1, YS2, YS3, YS4, YS5, YS6, YS7, YS8, YS9;
  wire [3:0] add_1_s, add_2_s, counter_1_out, counter_2_out, xAccum_q, xSpeed_q, yAccum_q, ySpeed_q;
  wire [9:0] ballX, ballY;

  xnor xnor_1 (xnor_1_out, ballX[0], H0);
  xnor xnor_2 (xnor_2_out, ballX[1], H1);
  xnor xnor_3 (xnor_3_out, ballX[2], H2);
  xnor xnor_4 (xnor_4_out, ballX[3], H3);
  xnor xnor_5 (xnor_5_out, ballX[4], H4);
  xnor xnor_6 (xnor_6_out, ballX[5], H5);
  xnor xnor_7 (xnor_7_out, ballX[6], H6);
  xnor xnor_8 (xnor_8_out, ballX[7], H7);
  xnor xnor_9 (xnor_9_out, ballX[8], H8);
  xnor xnor_10 (xnor_10_out, ballY[0], V0);
  xnor xnor_11 (xnor_11_out, ballY[1], V1);
  xnor xnor_12 (xnor_12_out, ballY[2], V2);
  xnor xnor_13 (xnor_13_out, ballY[3], V3);
  xnor xnor_14 (xnor_14_out, ballY[4], V4);
  xnor xnor_15 (xnor_15_out, ballY[5], V5);
  xnor xnor_16 (xnor_16_out, ballY[6], V6);
  xnor xnor_17 (xnor_17_out, ballY[7], V7);
  xnor xnor_18 (xnor_18_out, ballY[8], V8);
  xnor xnor_19 (xnor_19_out, ballY[9], V9);
  and and_1 (and_1_out, xnor_18_out, xnor_19_out);
  nand nand_1 (nand_1_out, xnor_1_out, xnor_2_out, xnor_3_out, xnor_4_out, xnor_5_out, xnor_6_out, xnor_7_out, xnor_8_out);
  nand nand_2 (nand_2_out, xnor_10_out, xnor_11_out, xnor_12_out, xnor_13_out, xnor_14_out, xnor_15_out, xnor_16_out, xnor_17_out);
  not not_1 (not_1_out, nand_1_out);
  not not_2 (not_2_out, nand_2_out);
  and and_2 (and_2_out, not_1_out, xnor_9_out);
  and and_3 (and_3_out, not_2_out, and_1_out);
  RS_FF_AS rs_ff_as_1 (.S(and_2_out), .R(counter_1_out[3]), .Q(rs_ff_as_1_q));  // open: nQ
  RS_FF_AS rs_ff_as_2 (.S(and_3_out), .R(counter_2_out[3]), .Q(rs_ff_as_2_q));  // open: nQ
  Counter #(.Bits(4)) counter_1 (
    .en(rs_ff_as_1_q), .C(Master_VGA_Clock), .clr(counter_1_out[3]), .out(counter_1_out));  // open: ovf
  Counter #(.Bits(4)) counter_2 (
    .en(rs_ff_as_2_q), .C(HCLR), .clr(counter_2_out[3]), .out(counter_2_out));  // open: ovf
  and and_4 (and_4_out, rs_ff_as_1_q, rs_ff_as_2_q);
  and and_5 (bR, and_4_out, ballR);
  RS_FF_AS XDir (.S(in_3), .R(in_4), .Q(XDir_q));  // open: nQ
  RS_FF_AS YDir (.S(in_3), .R(in_4), .Q(YDir_q));  // open: nQ
  Button A (.out(A_out));
  Register #(.Bits(4)) xSpeed (.D(4'b1100), .C(Ball_CLK), .en(1'b1), .Q(xSpeed_q));
  Register #(.Bits(4)) ySpeed (.D(4'b0100), .C(Ball_CLK), .en(1'b1), .Q(ySpeed_q));
  RS_FF_AS u_ballR (.S(A_out), .R(1'b0), .Q(ballR));  // open: nQ
  Add #(.Bits(4)) add_1 (.a(xAccum_q), .b(xSpeed_q), .c_i(1'b0), .s(add_1_s), .c_o(add_1_c_o));
  Add #(.Bits(4)) add_2 (.a(yAccum_q), .b(ySpeed_q), .c_i(1'b0), .s(add_2_s), .c_o(add_2_c_o));
  Register #(.Bits(4)) xAccum (.D(add_1_s), .C(Ball_CLK), .en(1'b1), .Q(xAccum_q));
  Register #(.Bits(4)) yAccum (.D(add_2_s), .C(Ball_CLK), .en(1'b1), .Q(yAccum_q));
  CounterPreset #(.Bits(10)) u_ballX (
    .en(1'b1), .C(add_1_c_o), .dir(XDir_q), .in(10'h13b), .ld(A_out), .clr(1'b0), .out(ballX));  // open: ovf
  CounterPreset #(.Bits(10)) u_ballY (
    .en(1'b1), .C(add_2_c_o), .dir(YDir_q), .in(10'h13b), .ld(A_out), .clr(1'b0), .out(ballY));  // open: ovf
  Button W (.out(LUP));
  Button S (.out(LDOW));
  not not_3 (not_3_out, RESET);
  not not_4 (not_4_out, START);
  or or_1 (B, MO, p1R, p2R, bR);
  _7474 _7474_1 (
    .pin1(not_3_out), .pin2(1'b0), .pin3(1'b0), .pin4(not_4_out), .pin5(RENDER), .pin7(1'b0), .pin10(1'b1),
    .pin11(1'b1), .pin12(1'b1), .pin13(1'b1), .pin14(1'b1));  // open: pin6, pin8, pin9
  Button I (.out(RUP));
  Button K (.out(RDOW));
  Button T (.out(START));
  Button Y (.out(RESET));
  VGA vga_1 (.R(B), .G(B), .B(B), .H(HSYNC), .V(VSYNC), .C(Master_VGA_Clock));
  _74163 _74163_1 (
    .pin1(HCLR), .pin2(Master_VGA_Clock), .pin3(1'b0), .pin4(1'b0), .pin5(1'b0), .pin6(1'b0), .pin7(1'b1),
    .pin8(1'b0), .pin9(1'b1), .pin10(1'b1), .pin11(H3), .pin12(H2), .pin13(H1), .pin14(H0),
    .pin15(_74163_1_pin15), .pin16(1'b1));
  _74163 _74163_2 (
    .pin1(HCLR), .pin2(Master_VGA_Clock), .pin3(1'b0), .pin4(1'b0), .pin5(1'b0), .pin6(1'b0), .pin7(1'b1),
    .pin8(1'b0), .pin9(1'b1), .pin10(_74163_1_pin15), .pin11(H7), .pin12(H6), .pin13(H5), .pin14(H4),
    .pin15(_74163_2_pin15), .pin16(1'b1));
  _74163 _74163_3 (
    .pin1(HCLR), .pin2(Master_VGA_Clock), .pin3(1'b0), .pin4(1'b0), .pin5(1'b0), .pin6(1'b0), .pin7(1'b1),
    .pin8(1'b0), .pin9(1'b1), .pin10(_74163_2_pin15), .pin11(H11), .pin12(H10), .pin13(H9), .pin14(H8),
    .pin16(1'b1));  // open: pin15
  _74193 _74193_1 (
    .pin1(YS1), .pin2(Y11), .pin3(Y10), .pin4(Y1U), .pin5(Y1D), .pin6(Y12), .pin7(Y13), .pin8(1'b0),
    .pin9(YS3), .pin10(YS2), .pin11(_74193_1_pin11), .pin12(_74193_1_pin12), .pin13(_74193_1_pin13),
    .pin14(1'b0), .pin15(YS0), .pin16(1'b1));
  _74193 _74193_2 (
    .pin1(YS5), .pin2(Y15), .pin3(Y14), .pin4(_74193_1_pin13), .pin5(_74193_1_pin12), .pin6(Y16), .pin7(Y17),
    .pin8(1'b0), .pin9(YS7), .pin10(YS6), .pin11(_74193_1_pin11), .pin12(_74193_2_pin12),
    .pin13(_74193_2_pin13), .pin14(1'b0), .pin15(YS4), .pin16(1'b1));
  _74193 _74193_3 (
    .pin1(YS9), .pin2(Y19), .pin3(Y18), .pin4(_74193_2_pin13), .pin5(_74193_2_pin12), .pin8(1'b0),
    .pin9(1'b0), .pin10(1'b0), .pin11(_74193_1_pin11), .pin14(1'b0), .pin15(YS8), .pin16(1'b1));  // open: pin6, pin7, pin12, pin13
  _74163 _74163_4 (
    .pin1(VCLR), .pin2(HCLR), .pin3(1'b0), .pin4(1'b0), .pin5(1'b0), .pin6(1'b0), .pin7(1'b1), .pin8(1'b0),
    .pin9(1'b1), .pin10(1'b1), .pin11(V3), .pin12(V2), .pin13(V1), .pin14(V0), .pin15(_74163_4_pin15),
    .pin16(1'b1));
  _74163 _74163_5 (
    .pin1(VCLR), .pin2(HCLR), .pin3(1'b0), .pin4(1'b0), .pin5(1'b0), .pin6(1'b0), .pin7(1'b1), .pin8(1'b0),
    .pin9(1'b1), .pin10(_74163_4_pin15), .pin11(V7), .pin12(V6), .pin13(V5), .pin14(V4),
    .pin15(_74163_5_pin15), .pin16(1'b1));
  _74163 _74163_6 (
    .pin1(VCLR), .pin2(HCLR), .pin3(1'b0), .pin4(1'b0), .pin5(1'b0), .pin6(1'b0), .pin7(1'b1), .pin8(1'b0),
    .pin9(1'b1), .pin10(_74163_5_pin15), .pin11(V11), .pin12(V10), .pin13(V9), .pin14(V8), .pin16(1'b1));  // open: pin15
  not not_5 (_74193_1_pin11, START);
  _7408 _7408_1 (
    .pin1(LUP), .pin2(Paddle), .pin3(_7408_1_pin3), .pin4(LDOW), .pin5(Paddle), .pin6(_7408_1_pin6),
    .pin7(1'b0), .pin8(_7408_1_pin8), .pin9(RUP), .pin10(Paddle), .pin11(_7408_1_pin11), .pin12(RDOW),
    .pin13(Paddle), .pin14(1'b1));
  not not_6 (Y1U, _7408_1_pin3);
  not not_7 (Y1D, _7408_1_pin6);
  not not_8 (Y2D, _7408_1_pin11);
  not not_9 (Y2U, _7408_1_pin8);
  _7430 _7430_1 (
    .pin1(H0), .pin2(H1), .pin3(H2), .pin4(H3), .pin5(H4), .pin6(_7430_1_pin6), .pin7(1'b0),
    .pin8(_7430_1_pin8), .pin11(_7430_1_pin11), .pin12(_7430_1_pin12), .pin14(1'b1));  // open: pin9, pin10, pin13
  not not_10 (_7430_1_pin6, H5);
  _7430 _7430_2 (
    .pin1(_7430_2_pin1), .pin2(_7430_2_pin2), .pin3(_7430_2_pin3), .pin4(_7430_2_pin4), .pin5(H4),
    .pin6(_7430_2_pin6), .pin7(1'b0), .pin8(_7430_2_pin8), .pin11(H7), .pin12(_7430_2_pin12), .pin14(1'b1));  // open: pin9, pin10, pin13
  not not_11 (_7430_2_pin1, H0);
  not not_12 (_7430_2_pin2, H1);
  not not_13 (_7430_2_pin3, H2);
  not not_14 (_7430_2_pin4, H3);
  not not_15 (_7430_2_pin6, H5);
  not not_16 (not_16_out, H8);
  _7408 _7408_2 (
    .pin1(not_16_out), .pin2(H9), .pin3(_7408_2_pin3), .pin4(_7408_2_pin4), .pin5(_7408_2_pin3),
    .pin6(_7408_2_pin6), .pin7(1'b0), .pin8(_7408_2_pin8), .pin9(_7408_2_pin9), .pin10(_7408_2_pin10),
    .pin11(_7408_2_pin9), .pin12(_7408_2_pin12), .pin13(H9), .pin14(1'b1));
  not not_17 (not_17_out, _7408_2_pin6);
  _7430 _7430_3 (
    .pin1(_7430_3_pin1), .pin2(_7430_3_pin2), .pin3(_7430_3_pin3), .pin4(_7430_3_pin4), .pin5(H4), .pin6(H5),
    .pin7(1'b0), .pin8(_7430_3_pin8), .pin11(H7), .pin12(H6), .pin14(1'b1));  // open: pin9, pin10, pin13
  not not_18 (_7430_3_pin1, H0);
  not not_19 (_7430_3_pin2, H1);
  not not_20 (_7430_3_pin3, H2);
  not not_21 (_7430_3_pin4, H3);
  not not_22 (not_22_out, _7430_1_pin8);
  not not_23 (_7408_2_pin4, _7430_2_pin8);
  not not_24 (not_24_out, _7408_2_pin8);
  not not_25 (_7408_2_pin10, _7430_3_pin8);
  not not_26 (_7430_1_pin12, H7);
  not not_27 (_7430_1_pin11, H6);
  not not_28 (_7430_2_pin12, H6);
  not not_29 (_7408_2_pin12, H8);
  _74193 _74193_4 (
    .pin1(YS1), .pin2(Y21), .pin3(Y20), .pin4(Y2U), .pin5(Y2D), .pin6(Y22), .pin7(Y23), .pin8(1'b0),
    .pin9(YS3), .pin10(YS2), .pin11(_74193_4_pin11), .pin12(_74193_4_pin12), .pin13(_74193_4_pin13),
    .pin14(1'b0), .pin15(YS0), .pin16(1'b1));
  _74193 _74193_5 (
    .pin1(YS5), .pin2(Y25), .pin3(Y24), .pin4(_74193_4_pin13), .pin5(_74193_4_pin12), .pin6(Y26), .pin7(Y27),
    .pin8(1'b0), .pin9(YS7), .pin10(YS6), .pin11(_74193_4_pin11), .pin12(_74193_5_pin12),
    .pin13(_74193_5_pin13), .pin14(1'b0), .pin15(YS4), .pin16(1'b1));
  _74193 _74193_6 (
    .pin1(YS9), .pin2(Y29), .pin3(Y28), .pin4(_74193_5_pin13), .pin5(_74193_5_pin12), .pin8(1'b0),
    .pin9(1'b0), .pin10(1'b0), .pin11(_74193_4_pin11), .pin14(1'b0), .pin15(YS8), .pin16(1'b1));  // open: pin6, pin7, pin12, pin13
  _7408 _7408_3 (
    .pin1(H8), .pin2(H9), .pin3(_7408_3_pin3), .pin4(not_22_out), .pin5(_7408_3_pin3), .pin6(_7408_3_pin6),
    .pin7(1'b0), .pin8(_7408_3_pin8), .pin9(_7408_3_pin9), .pin10(V9), .pin11(_7408_3_pin11),
    .pin12(_7408_3_pin12), .pin13(_7408_3_pin8), .pin14(1'b1));
  not not_30 (HCLR, _7408_3_pin6);
  _7474 _7474_2 (
    .pin1(not_17_out), .pin2(1'b0), .pin3(1'b0), .pin4(not_24_out), .pin5(HSYNC), .pin7(1'b0), .pin9(VSYNC),
    .pin10(_7474_2_pin10), .pin11(1'b0), .pin12(1'b0), .pin13(_7474_2_pin13), .pin14(1'b1));  // open: pin6, pin8
  not not_31 (VCLR, _7408_3_pin11);
  not not_32 (_7408_3_pin9, V8);
  not not_33 (_74193_4_pin11, START);
  _7430 _7430_4 (
    .pin1(_7430_4_pin1), .pin2(_7430_4_pin2), .pin3(V2), .pin4(V3), .pin5(_7430_4_pin5), .pin6(_7430_4_pin6),
    .pin7(1'b0), .pin8(_7430_4_pin8), .pin11(_7430_4_pin11), .pin12(_7430_4_pin12), .pin14(1'b1));  // open: pin9, pin10, pin13
  not not_34 (_7430_4_pin1, V0);
  not not_35 (_7430_4_pin2, V1);
  not not_36 (_7430_4_pin5, V4);
  not not_37 (_7430_4_pin6, V5);
  not not_38 (not_38_out, V0);
  not not_39 (not_39_out, V2);
  not not_40 (not_40_out, V4);
  not not_41 (not_41_out, V9);
  not not_42 (not_42_out, V0);
  not not_43 (not_43_out, V1);
  not not_44 (not_44_out, V4);
  _7430 _7430_5 (
    .pin1(not_38_out), .pin2(V1), .pin3(not_39_out), .pin4(V3), .pin5(not_40_out), .pin6(V5), .pin7(1'b0),
    .pin8(_7430_5_pin8), .pin11(V7), .pin12(V6), .pin14(1'b1));  // open: pin9, pin10, pin13
  _7408 _7408_4 (
    .pin1(V8), .pin2(not_41_out), .pin3(_7408_4_pin3), .pin4(_7408_4_pin4), .pin5(_7408_4_pin3),
    .pin6(_7408_4_pin6), .pin7(1'b0), .pin8(_7408_4_pin8), .pin9(_7408_4_pin9), .pin10(_7408_4_pin10),
    .pin11(_7408_4_pin10), .pin12(_7408_4_pin12), .pin13(V8), .pin14(1'b1));
  not not_45 (_7474_2_pin13, _7408_4_pin6);
  _7430 _7430_6 (
    .pin1(not_42_out), .pin2(not_43_out), .pin3(V2), .pin4(V3), .pin5(not_44_out), .pin6(V5), .pin7(1'b0),
    .pin8(_7430_6_pin8), .pin11(V7), .pin12(V6), .pin14(1'b1));  // open: pin9, pin10, pin13
  not not_46 (_7408_3_pin12, _7430_4_pin8);
  not not_47 (_7430_4_pin12, V7);
  not not_48 (_7430_4_pin11, V6);
  not not_49 (_7408_4_pin4, _7430_5_pin8);
  not not_50 (_7408_4_pin12, V9);
  not not_51 (_7474_2_pin10, _7408_4_pin8);
  not not_52 (_7408_4_pin9, _7430_6_pin8);
  not not_53 (not_53_out, H0);
  not not_54 (not_54_out, H1);
  not not_55 (not_55_out, H2);
  not not_56 (not_56_out, H3);
  not not_57 (not_57_out, H4);
  not not_58 (not_58_out, H5);
  _7430 _7430_7 (
    .pin1(not_53_out), .pin2(not_54_out), .pin3(not_55_out), .pin4(not_56_out), .pin5(not_57_out),
    .pin6(not_58_out), .pin7(1'b0), .pin8(_7430_7_pin8), .pin11(H6), .pin12(_7430_7_pin12), .pin14(1'b1));  // open: pin9, pin10, pin13
  not not_59 (_7430_7_pin12, H7);
  not not_60 (not_60_out, _7430_7_pin8);
  _747266 _747266_1 (
    .pin1(H3), .pin2(1'b0), .pin3(_747266_1_pin3), .pin4(_747266_1_pin4), .pin5(H4), .pin6(1'b1),
    .pin7(1'b0), .pin8(H5), .pin9(1'b0), .pin10(_747266_1_pin10), .pin11(_747266_1_pin11), .pin12(H6),
    .pin13(1'b0), .pin14(1'b1));
  _747266 _747266_2 (
    .pin1(H7), .pin2(1'b0), .pin3(_747266_2_pin3), .pin4(_747266_2_pin4), .pin5(H8), .pin6(1'b0),
    .pin7(1'b0), .pin8(H9), .pin9(1'b0), .pin10(_747266_2_pin10), .pin11(_747266_2_pin11), .pin12(V5),
    .pin13(Y15), .pin14(1'b1));
  _747266 _747266_3 (
    .pin1(V6), .pin2(Y16), .pin3(_747266_3_pin3), .pin4(_747266_3_pin4), .pin5(V7), .pin6(Y17), .pin7(1'b0),
    .pin8(V9), .pin9(Y19), .pin10(_747266_3_pin10), .pin11(_747266_3_pin11), .pin12(V8), .pin13(Y18),
    .pin14(1'b1));
  _7408 _7408_5 (
    .pin1(H8), .pin2(_7408_5_pin2), .pin3(_7408_5_pin3), .pin4(not_60_out), .pin5(_7408_5_pin3),
    .pin6(_7408_5_pin6), .pin7(1'b0), .pin8(MO), .pin9(_7408_5_pin9), .pin10(_7408_5_pin6),
    .pin11(_7408_5_pin9), .pin12(V3), .pin13(1'b1), .pin14(1'b1));
  not not_61 (_7408_5_pin2, H9);
  _7430 _7430_8 (
    .pin1(_747266_1_pin3), .pin2(_747266_1_pin4), .pin3(_747266_1_pin11), .pin4(_747266_1_pin10),
    .pin5(_747266_2_pin3), .pin6(_747266_2_pin4), .pin7(1'b0), .pin8(_7430_8_pin8), .pin11(1'b1),
    .pin12(_747266_2_pin10), .pin14(1'b1));  // open: pin9, pin10, pin13
  _7430 _7430_9 (
    .pin1(_747266_2_pin11), .pin2(_747266_3_pin3), .pin3(_747266_3_pin4), .pin4(_747266_3_pin11),
    .pin5(_747266_3_pin10), .pin6(_747266_3_pin10), .pin7(1'b0), .pin8(_7430_9_pin8), .pin11(1'b1),
    .pin12(1'b1), .pin14(1'b1));  // open: pin9, pin10, pin13
  not not_62 (p1rx, _7430_8_pin8);
  _74163 _74163_7 (
    .pin1(_74163_7_pin1), .pin2(HCLR), .pin3(1'b0), .pin4(1'b0), .pin5(1'b0), .pin6(1'b0), .pin7(p1ry),
    .pin8(1'b0), .pin9(p1ry), .pin10(p1ry), .pin15(_74163_7_pin15), .pin16(1'b1));  // open: pin11, pin12, pin13, pin14
  _74163 _74163_8 (
    .pin1(_74163_7_pin1), .pin2(HCLR), .pin3(1'b0), .pin4(1'b0), .pin5(1'b0), .pin6(1'b0), .pin7(p1ry),
    .pin8(1'b0), .pin9(p1ry), .pin10(_74163_7_pin15), .pin12(_74163_8_pin12), .pin16(1'b1));  // open: pin11, pin13, pin14, pin15
  not not_63 (_74163_7_pin1, _74163_8_pin12);
  _7474 _7474_3 (
    .pin1(_74163_7_pin1), .pin2(1'b0), .pin3(1'b0), .pin4(_7430_9_pin8), .pin5(p1ry), .pin7(1'b0),
    .pin9(p2ry), .pin10(_7474_3_pin10), .pin11(1'b0), .pin12(1'b0), .pin13(_7474_3_pin13), .pin14(1'b1));  // open: pin6, pin8
  _7408 _7408_6 (
    .pin1(p1ry), .pin2(p1rx), .pin3(_7408_6_pin3), .pin4(_7408_6_pin3), .pin5(RENDER), .pin6(p1R),
    .pin7(1'b0), .pin8(_7408_6_pin8), .pin9(p2rx), .pin10(p2ry), .pin11(p2R), .pin12(_7408_6_pin8),
    .pin13(RENDER), .pin14(1'b1));
  _74163 _74163_9 (
    .pin1(_7474_3_pin13), .pin2(HCLR), .pin3(1'b0), .pin4(1'b0), .pin5(1'b0), .pin6(1'b0), .pin7(p2ry),
    .pin8(1'b0), .pin9(p2ry), .pin10(p2ry), .pin15(_74163_9_pin15), .pin16(1'b1));  // open: pin11, pin12, pin13, pin14
  _74163 _74163_10 (
    .pin1(_7474_3_pin13), .pin2(HCLR), .pin3(1'b0), .pin4(1'b0), .pin5(1'b0), .pin6(1'b0), .pin7(p2ry),
    .pin8(1'b0), .pin9(p2ry), .pin10(_74163_9_pin15), .pin12(_74163_10_pin12), .pin16(1'b1));  // open: pin11, pin13, pin14, pin15
  not not_64 (_7474_3_pin13, _74163_10_pin12);
  _7430 _7430_10 (
    .pin1(_7430_10_pin1), .pin2(_7430_10_pin2), .pin3(_7430_10_pin3), .pin4(_7430_10_pin4),
    .pin5(_7430_10_pin5), .pin6(_7430_10_pin6), .pin7(1'b0), .pin8(_7430_10_pin8), .pin11(_7430_10_pin11),
    .pin12(1'b1), .pin14(1'b1));  // open: pin9, pin10, pin13
  _7430 _7430_11 (
    .pin1(_7430_11_pin1), .pin2(_7430_11_pin2), .pin3(_7430_11_pin3), .pin4(_7430_11_pin4),
    .pin5(_7430_11_pin5), .pin6(_7430_11_pin5), .pin7(1'b0), .pin8(_7474_3_pin10), .pin11(1'b1),
    .pin12(1'b1), .pin14(1'b1));  // open: pin9, pin10, pin13
  not not_65 (p2rx, _7430_10_pin8);
  _747266 _747266_4 (
    .pin1(H3), .pin2(1'b0), .pin3(_7430_10_pin1), .pin4(_7430_10_pin2), .pin5(H4), .pin6(1'b0), .pin7(1'b0),
    .pin8(H5), .pin9(1'b1), .pin10(_7430_10_pin4), .pin11(_7430_10_pin3), .pin12(H6), .pin13(1'b1),
    .pin14(1'b1));
  _747266 _747266_5 (
    .pin1(H7), .pin2(1'b0), .pin3(_7430_10_pin5), .pin4(_7430_10_pin6), .pin5(H8), .pin6(1'b0), .pin7(1'b0),
    .pin8(H9), .pin9(1'b1), .pin10(_7430_10_pin11), .pin11(_7430_11_pin1), .pin12(V5), .pin13(Y25),
    .pin14(1'b1));
  _747266 _747266_6 (
    .pin1(V6), .pin2(Y26), .pin3(_7430_11_pin2), .pin4(_7430_11_pin3), .pin5(V7), .pin6(Y27), .pin7(1'b0),
    .pin8(V9), .pin9(Y29), .pin10(_7430_11_pin5), .pin11(_7430_11_pin4), .pin12(V8), .pin13(Y28), .pin14(1'b1));
  // also tied to GND on the sheet: {YS0, YS1, YS2, YS3, YS5, YS8, YS9}
  // also tied to VCC on the sheet: {YS4, YS6, YS7}

  // Other names for the same wires on the sheet: CLK = Master_VGA_Clock;
  //   HCOUNT[9:0] = {H9, H8, H7, H6, H5, H4, H3, H2, H1, H0}; PCLK = Paddle; G = B; R = B;
  //   VCOUNT[9:0] = {V9, V8, V7, V6, V5, V4, V3, V2, V1, V0};
  //   YSTART[9:0] = {YS9, YS8, YS7, YS6, YS5, YS4, YS3, YS2, YS1, YS0}

  // Notes on the sheet:
  //   Master_VGA_Clock: Hz: 10175000
  //   Paddle: Hz: 240
  //   Ball_CLK: Hz: 600
  //   I/O SUITE
  //   COUNTERS
  //   VGA DRIVER
  //   CLR
  //   SYNC GEN
  //   PARTING (STATIC)
endmodule
